// Logisim project cpu.circ as structural Verilog: 1 circuit, main circuit main
module main (
  input  [31:0] INSTRUCTION,
  input  CLOCK,
  output [31:0] PROGRAM_COUNTER,
  output [31:0] ra,
  output [31:0] sp,
  output [31:0] t0,
  output [31:0] t1,
  output [31:0] t2,
  output [31:0] s0,
  output [31:0] s1,
  output [31:0] a0
);

  wire control_logic_1_bsel, control_logic_1_regwen, RegFile_p8;
  wire [2:0] control_logic_1_immsel;
  wire [3:0] control_logic_1_alusel;
  wire [31:0] adder_1_out, imm_gen_1_imm, INS_OUT, multiplexer_1_out, RegFile_p9, wb;

  control_logic control_logic_1 (
    .BSel(control_logic_1_bsel), .RegWEn(control_logic_1_regwen), .ImmSel(control_logic_1_immsel),
    .inst(INS_OUT), .ALUSel(control_logic_1_alusel));  // open: BrUn, ASel, PCSel, BrLt, BrEq, MemRW, WBSel
  Adder #(.width(32)) adder_1 (.a(PROGRAM_COUNTER), .b(32'h4), .out(adder_1_out));  // open: cin, cout
  Register #(.width(32)) PC (.D(adder_1_out), .clk(CLOCK), .Q(PROGRAM_COUNTER));  // open: en, clr
  imm_gen imm_gen_1 (.ImmSel(control_logic_1_immsel), .inst(INS_OUT), .imm(imm_gen_1_imm));
  Register #(.width(32)) IReg (.D(INSTRUCTION), .clk(CLOCK), .Q(INS_OUT));  // open: en, clr
  // branch_comp branch_comp_1: pin names not known; wires that end beside it: INS_OUT[19:15], INS_OUT[24:20], INS_OUT[11:7], wb
  // regfile_main RegFile: pin names not known; wires that end beside it: t0, t1, t2, s0, control_logic_1_regwen, s1, a0, RegFile_p8, RegFile_p9
  Multiplexer #(.width(32), .enable("false")) multiplexer_1 (
    .in0(RegFile_p9), .in1(imm_gen_1_imm), .out(multiplexer_1_out), .sel(control_logic_1_bsel));
  // alu Arithmetic_Logic_Unit: pin names not known; wires that end beside it: RegFile_p8, multiplexer_1_out, control_logic_1_alusel, wb
  // mem_main DMEM: pin names not known

  // Other names for the same wires on the sheet: clk = CLOCK

  // Notes on the sheet:
  //   Output
  //   IMEM (do **NOT** move this)
  //   Inputs
  //   It is OK to move the PC, RegFile, ALU, MEM, Branch Comp, Imm Gen, and Control Logic to wherever is most convenient for you when constructing your CPU, and to delete this text
  //   Inputs/Outputs for testing. Do **NOT** move these.
endmodule
